# Fritzing sketch deye-esp-mqtt-bridge_V1 (saved by Fritzing 1.0.1rc)
breadboards: 1

parts:
  WeMos_D1_Mini1 = WeMos D1 Mini
  OLED_128x32 = OLED Monochrome 128x32 I2C [part_number=931]

nets:
  3V3: WeMos_D1_Mini1.3V3, OLED_128x32.3.3V
  N1: WeMos_D1_Mini1.D1, OLED_128x32.SCL
  N2: WeMos_D1_Mini1.D2, OLED_128x32.SDA
  N3: WeMos_D1_Mini1.G, OLED_128x32.GND

custom parts:
  OLED Monochrome 128x32 I2C: These displays are small, only about 1" diagonal, but very readable due to the high contrast of an OLED display. This display is made of 128x32 individual white OLED pixels, each one is turned on or off by the controller chip. Because the display makes its own light, no backlight is required. This reduces the power required to run the OLED and is why the display has such high contrast; we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
